# Fritzing sketch anslutning_av_en_lysdiod (saved by Fritzing 0.9.6b)
breadboards: 17

parts:
  A2 = Arduino Uno (Rev3)
  R2 = Resistor [tolerance=±5% power=0.25 resistance=1k package=THT]
  LED2 = LED - 5mm [color="Red (633nm)" current=0.030 package="5 mm [THT]"]
  A6 = Arduino Uno (Rev3)
  LED6 = LED - 5mm [color="Red (633nm)" current=0.030 package="5 mm [THT]"]
  R6 = Resistor [tolerance=±5% power=0.25 resistance=1k package=THT]
  A7 = Arduino Uno (Rev3)
  A8 = Arduino Uno (Rev3)
  LED7 = LED - 5mm [color="Red (633nm)" current=0.030 package="5 mm [THT]"]
  LED8 = LED - 5mm [color="Red (633nm)" current=0.030 package="5 mm [THT]"]
  R7 = Resistor [tolerance=±5% power=0.25 resistance=1k package=THT]
  R8 = Resistor [tolerance=±5% power=0.25 resistance=1k package=THT]
  A9 = Arduino Uno (Rev3)  # not connected
  LED9 = LED - 5mm [color="Red (633nm)" current=0.030 package="5 mm [THT]"]  # not connected
  R9 = Resistor [tolerance=±5% power=0.25 resistance=1k package=THT]  # not connected
  A10 = Arduino Uno (Rev3)
  LED10 = LED - 5mm [color="Red (633nm)" current=0.030 package="5 mm [THT]"]
  R10 = Resistor [tolerance=±5% power=0.25 resistance=1k package=THT]
  A11 = Arduino Uno (Rev3)
  LED11 = LED - 5mm [color="Red (633nm)" current=0.030 package="5 mm [THT]"]
  R11 = Resistor [tolerance=±5% power=0.25 resistance=1k package=THT]
  A12 = Arduino Uno (Rev3)
  LED12 = LED - 5mm [color="Red (633nm)" current=0.030 package="5 mm [THT]"]
  R12 = Resistor [tolerance=±5% power=0.25 resistance=1k package=THT]
  A13 = Arduino Uno (Rev3)
  LED13 = LED - 5mm [color="Red (633nm)" current=0.030 package="5 mm [THT]"]
  R13 = Resistor [tolerance=±5% power=0.25 resistance=1k package=THT]
  A14 = Arduino Uno (Rev3)
  LED14 = LED - 5mm [color="Red (633nm)" current=0.030 package="5 mm [THT]"]
  R14 = Resistor [tolerance=±5% power=0.25 resistance=1k package=THT]
  A15 = Arduino Uno (Rev3)
  LED15 = LED - 5mm [color="Red (633nm)" current=0.030 package="5 mm [THT]"]
  R15 = Resistor [tolerance=±5% power=0.25 resistance=1k package=THT]
  A16 = Arduino Uno (Rev3)
  LED16 = LED - 5mm [color="Red (633nm)" current=0.030 package="5 mm [THT]"]
  R16 = Resistor [tolerance=±5% power=0.25 resistance=1k package=THT]
  A17 = Arduino Uno (Rev3)
  LED17 = LED - 5mm [color="Red (633nm)" current=0.030 package="5 mm [THT]"]
  R17 = Resistor [tolerance=±5% power=0.25 resistance=1k package=THT]
  A18 = Arduino Uno (Rev3)
  LED19 = LED - 5mm [color="Red (633nm)" current=0.030 package="5 mm [THT]"]
  R18 = Resistor [tolerance=±5% power=0.25 resistance=1k package=THT]
  A19 = Arduino Uno (Rev3)
  LED20 = LED - 5mm [color="Red (633nm)" current=0.030 package="5 mm [THT]"]
  R19 = Resistor [tolerance=±5% power=0.25 resistance=1k package=THT]
  A20 = Arduino Uno (Rev3)
  LED21 = LED - 5mm [color="Red (633nm)" current=0.030 package="5 mm [THT]"]
  R20 = Resistor [tolerance=±5% power=0.25 resistance=1k package=THT]

nets:
  N1: A2.5V, LED2.anode
  N2: A2.GND, R2.Pin_1
  N3: R2.Pin_0, LED2.cathode
  N4: A6.5V, LED6.cathode
  N5: A6.GND, R6.Pin_1
  N6: LED6.anode, R6.Pin_0
  N7: A7.5V, LED8.anode
  N8: A7.GND, R8.Pin_0
  N9: A8.5V, LED7.cathode
  N10: A8.GND, R7.Pin_0
  N11: LED7.anode, R7.Pin_1
  N12: LED8.cathode, R8.Pin_1
  N13: A10.5V, LED10.anode
  N14: A10.GND, R10.Pin_1
  N15: LED10.cathode, R10.Pin_0
  N16: A11.5V, LED11.anode
  N17: A11.GND, R11.Pin_1
  N18: LED11.cathode, R11.Pin_0
  N19: A12.5V, LED12.anode
  N20: A12.GND, R12.Pin_1
  N21: LED12.cathode, R12.Pin_0
  N22: A13.5V, LED13.anode, R13.Pin_0
  N23: A13.GND, R13.Pin_1
  N24: A14.5V, LED14.cathode
  N25: A14.GND, R14.Pin_1
  N26: LED14.anode, R14.Pin_0
  N27: A15.5V, R15.Pin_0
  N28: A15.GND, LED15.anode
  N29: LED15.cathode, R15.Pin_1
  N30: A16.5V, R16.Pin_0
  N31: A16.GND, LED16.anode
  N32: LED16.cathode, R16.Pin_1
  N33: A17.5V, R17.Pin_0
  N34: A17.GND, LED17.anode
  N35: LED17.cathode, R17.Pin_1
  N36: A18.5V, LED19.cathode
  N37: A18.GND, R18.Pin_1
  N38: LED19.anode, R18.Pin_0
  N39: A19.5V, LED20.cathode
  N40: A19.GND, R19.Pin_1
  N41: LED20.anode, R19.Pin_0
  N42: A20.5V, LED21.cathode
  N43: A20.GND, R20.Pin_0
  N44: LED21.anode, R20.Pin_1
