# Fritzing sketch anslutning_av_en_joystick (saved by Fritzing 0.9.6b)
breadboards: 1

parts:
  Part2 = Arduino Uno (Rev3)
  joystick1 = Black Joystick KY-023
  LED1 = RGB LED (com. cathode, rgb) [package="5 mm [THT]"]
  R1 = Resistor [tolerance=±5% resistance=1k package="2010 [SMD]"]
  R2 = Resistor [tolerance=±5% resistance=1k package="2010 [SMD]"]
  R3 = Resistor [tolerance=±5% resistance=1k package="2010 [SMD]"]

nets:
  5V: Part2.5V, joystick1.+5V
  GND: Part2.GND, joystick1.GND
  N1: LED1.red_anode, R1.Pin_1
  N2: LED1.green_anode, R2.Pin_1
  N3: LED1.blue_anode, R3.Pin_1

notes:
  Joystick from
  https://github.com/peyretti/My-Templates-Fritzing
  or its Fork at
  https://github.com/richelbilderbeek/My-Templates-Fritzing

custom parts:
  Black Joystick KY-023: Description: The joystick is a combination of 2 analoog potentiometer and a digital switch. Arduino GND --> Module pin - Arduino +5V --> Module pin +5V Arduino Analoog 0 --> Module VRx Arduino Analoog 1 --> Module VRy Arduino Digital --> Module SW Dimensions: 1" x 1.25"
