# Fritzing sketch ky-038_microfon (saved by Fritzing 0.9.6b)
breadboards: 1

parts:
  Mic1 = KY-038
  Part1 = Arduino Uno (Rev3)

nets:
  N1: Mic1.pin1, Part1.A0
  N2: Mic1.pin2, Part1.GND
  N3: Mic1.pin3, Part1.5V

custom parts:
  KY-038: ky-038 Microphone sound sensor module
